// Logisim project cpu.circ as structural Verilog: 5 circuits, main circuit main
module main (
);

  wire clock_1_out, clock_2_out;
  wire [2:2] multiplexer_1_out;
  wire [3:0] register_3_q, register_4_q;
  wire [4:0] register_2_q, rom_2_data_2;
  wire [7:0] datapath_1_abh_2, datapath_1_abl_2, datapath_1_dout, datapath_1_preg, ram_1_data, register_1_q;
  wire [31:0] rom_1_data, rom_2_data;

  Clock clock_1 (.out(clock_1_out));
  Register #(.trigger("falling")) register_1 (
    .D(datapath_1_dout), .en(rom_2_data[10]), .Q(register_1_q), .clk(clock_1_out), .clr(1'b0));
  Register #(.width(5), .trigger("falling")) register_2 (
    .D(rom_2_data_2), .en(1'b1), .Q(register_2_q), .clk(clock_1_out), .clr(1'b0));
  Register #(.width(4), .trigger("falling")) register_3 (
    .D(register_4_q), .en(1'b1), .Q(register_3_q), .clk(clock_1_out));  // open: clr
  Register #(.width(4)) register_4 (
    .D({1'b0, multiplexer_1_out[2], 2'b00}), .en(1'b1), .Q(register_4_q), .clk(clock_1_out));  // open: clr
  // Probe on ram_1_data
  ROM #(.addrWidth(17), .dataWidth(32)) rom_1 (
    .addr({register_1_q, register_2_q, register_3_q}), .data(rom_1_data));  // open: sel
  ROM #(.addrWidth(17), .dataWidth(32)) rom_2 (
    .addr({register_1_q, register_2_q, register_3_q}),
    .data({rom_2_data[31:16], rom_2_data_2, rom_2_data[10:0]}));  // open: sel
  // Probe on datapath_1_dout
  // Probe on {datapath_1_abh_2, datapath_1_abl_2}
  datapath datapath_1 (
    .ALUF(rom_1_data[5:0]), .IB(rom_1_data[9:6]), .ALUCIN(rom_1_data[11:10]), .ABL(rom_1_data[14:12]),
    .PC_1(rom_1_data[15]), .OB(rom_1_data[19:16]), .ABH(rom_1_data[22:20]), .FLAGS(rom_2_data[9:0]),
    .DIN(ram_1_data), .DOUT(datapath_1_dout), .ABL_2(datapath_1_abl_2), .ABH_2(datapath_1_abh_2),
    .PREG(datapath_1_preg));
  Multiplexer #(.select(4), .enable("false")) multiplexer_1 (
    .in0(1'b0), .in1(datapath_1_preg[0]), .in2(datapath_1_preg[1]), .in3(datapath_1_preg[2]),
    .in4(datapath_1_preg[6]), .in5(datapath_1_preg[7]), .in6(datapath_1_preg[3]), .out(multiplexer_1_out[2]),
    .sel(rom_2_data[19:16]));  // open: in7, in8, in9, in10, in11, in12, in13, in14, in15
  Clock clock_2 (.out(clock_2_out));
  RAM #(.addrWidth(16), .bus("asynch")) ram_1 (
    .addr({datapath_1_abh_2, datapath_1_abl_2}), .data(ram_1_data), .sel(1'b1), .ld(1'b1), .clr(1'b0));

  // Notes on the sheet:
  //   contents of rom_1 (hex, n*v repeats v):
  //   9825a 0 0 0 9825a 0 0 0 9825a 0 0 0 9825a 499*0 9825a 0 0 0 9825a 0 0 0 9825a 0 0 0 9825a 499*0
  //   9825a 0 0 0 9825a 0 0 0 9825a 0 0 0 9825a 499*0 9825a 0 0 0 9825a 0 0 0 9825a 0 0 0 9825a 499*0
  //   9825a 0 0 0 9825a 0 0 0 9825a 0 0 0 9825a 499*0 9825a 0 0 0 9825a 0 0 0 9825a 0 0 0 9825a 499*0
  //   9825a 0 0 0 9825a 0 0 0 9825a 0 0 0 9825a 499*0 9825a 0 0 0 9825a 0 0 0 9825a 0 0 0 9825a 499*0
  //   9825a 0 0 0 9825a 0 0 0 9825a 0 0 0 9825a 499*0 9825a 0 0 0 9825a 0 0 0 9825a 0 0 0 9825a 499*0
  //   9825a 0 0 0 9825a 0 0 0 9825a 0 0 0 9825a 499*0 9825a 0 0 0 9825a 0 0 0 9825a 0 0 0 9825a 499*0
  //   9825a 0 0 0 9825a 0 0 0 9825a 0 0 0 9825a 499*0 9825a 0 0 0 9825a 0 0 0 9825a 0 0 0 9825a 499*0
  //   9825a 0 0 0 9825a 0 0 0 9825a 0 0 0 9825a 499*0 9825a 0 0 0 9825a 0 0 0 9825a 0 0 0 9825a 499*0
  //   9825a 0 0 0 9825a 0 0 0 9825a 0 0 0 9825a 499*0 9825a 0 0 0 9825a 0 0 0 9825a 0 0 0 9825a 499*0
  //   9825a 0 0 0 9825a 0 0 0 9825a 0 0 0 9825a 499*0 9825a 0 0 0 9825a 0 0 0 9825a 0 0 0 9825a 499*0
  //   9825a 0 0 0 9825a 0 0 0 9825a 0 0 0 9825a 499*0 9825a 0 0 0 9825a 0 0 0 9825a 0 0 0 9825a 499*0
  //   9825a 0 0 0 9825a 0 0 0 9825a 0 0 0 9825a 499*0 9825a 0 0 0 9825a 0 0 0 9825a 0 0 0 9825a 499*0
  //   9825a 0 0 0 9825a 0 0 0 9825a 0 0 0 9825a 499*0 9825a 0 0 0 9825a 0 0 0 9825a 0 0 0 9825a 499*0
  //   9825a 0 0 0 9825a 0 0 0 9825a 0 0 0 9825a 499*0 9825a 0 0 0 9825a 0 0 0 9825a 0 0 0 9825a 499*0
  //   9825a 0 0 0 9825a 0 0 0 9825a 0 0 0 9825a 499*0 9825a 0 0 0 9825a 0 0 0 9825a 0 0 0 9825a 499*0
  //   9825a 0 0 0 9825a 0 0 0 9825a 0 0 0 9825a 499*0 9825a 0 0 0 9825a 0 0 0 9825a 0 0 0 9825a 499*0
  //   9825a 0 0 0 9825a 0 0 0 9825a 0 0 0 9825a 499*0 9825a 0 0 0 9825a 0 0 0 9825a 0 0 0 9825a 499*0
  //   9825a 0 0 0 9825a 0 0 0 9825a 0 0 0 9825a 499*0 9825a 0 0 0 9825a 0 0 0 9825a 0 0 0 9825a 499*0
  //   9825a 0 0 0 9825a 0 0 0 9825a 0 0 0 9825a 499*0 9825a 0 0 0 9825a 0 0 0 9825a 0 0 0 9825a 499*0
  //   9825a 0 0 0 9825a 0 0 0 9825a 0 0 0 9825a 499*0 9825a 0 0 0 9825a 0 0 0 9825a 0 0 0 9825a 499*0
  //   9825a 0 0 0 9825a 0 0 0 9825a 0 0 0 9825a 499*0 9825a 0 0 0 9825a 0 0 0 9825a 0 0 0 9825a 499*0
  //   9825a 0 0 0 9825a 0 0 0 9825a 0 0 0 9825a 499*0 9825a 0 0 0 9825a 0 0 0 9825a 0 0 0 9825a 499*0
  //   9825a 0 0 0 9825a 0 0 0 9825a 0 0 0 9825a 499*0 9825a 0 0 0 9825a 0 0 0 9825a 0 0 0 9825a 499*0
  //   9825a 0 0 0 9825a 0 0 0 9825a 0 0 0 9825a 499*0 9825a 0 0 0 9825a 0 0 0 9825a 0 0 0 9825a 499*0
  //   9825a 0 0 0 9825a 0 0 0 9825a 0 0 0 9825a 499*0 9825a 0 0 0 9825a 0 0 0 9825a 0 0 0 9825a 499*0
  //   9825a 0 0 0 9825a 0 0 0 9825a 0 0 0 9825a 499*0 9825a 0 0 0 9825a 0 0 0 9825a 0 0 0 9825a 499*0
  //   9825a 0 0 0 9825a 0 0 0 9825a 0 0 0 9825a 499*0 9825a 0 0 0 9825a 0 0 0 9825a 0 0 0 9825a 499*0
  //   9825a 0 0 0 9825a 0 0 0 9825a 0 0 0 9825a 499*0 9825a 0 0 0 9825a 0 0 0 9825a 0 0 0 9825a 499*0
  //   9825a 0 0 0 9825a 0 0 0 9825a 0 0 0 9825a 499*0 9825a 0 0 0 9825a 0 0 0 9825a 0 0 0 9825a 499*0
  //   9825a 0 0 0 9825a 0 0 0 9825a 0 0 0 9825a 499*0 9825a 0 0 0 9825a 0 0 0 9825a 0 0 0 9825a 499*0
  //   9825a 0 0 0 9825a 0 0 0 9825a 0 0 0 9825a 499*0 9825a 0 0 0 9825a 0 0 0 9825a 0 0 0 9825a 499*0
  //   9825a 0 0 0 9825a 0 0 0 9825a 0 0 0 9825a 499*0 9825a 0 0 0 9825a 0 0 0 9825a 0 0 0 9825a 499*0
  //   9825a 0 0 0 9825a 0 0 0 9825a 0 0 0 9825a 499*0 9825a 0 0 0 9825a 0 0 0 9825a 0 0 0 9825a 499*0
  //   9825a 0 0 0 9825a 0 0 0 9825a 0 0 0 9825a 499*0 9825a 0 0 0 9825a 0 0 0 9825a 0 0 0 9825a 499*0
  //   9825a 0 0 0 9825a 0 0 0 9825a 0 0 0 9825a 499*0 9825a 0 0 0 9825a 0 0 0 9825a 0 0 0 9825a 499*0
  //   9825a 0 0 0 9825a 0 0 0 9825a 0 0 0 9825a 499*0 9825a 0 0 0 9825a 0 0 0 9825a 0 0 0 9825a 499*0
  //   9825a 0 0 0 9825a 0 0 0 9825a 0 0 0 9825a 499*0 9825a 0 0 0 9825a 0 0 0 9825a 0 0 0 9825a 499*0
  //   9825a 0 0 0 9825a 0 0 0 9825a 0 0 0 9825a 499*0 9825a 0 0 0 9825a 0 0 0 9825a 0 0 0 9825a 499*0
  //   9825a 0 0 0 9825a 0 0 0 9825a 0 0 0 9825a 499*0 9825a 0 0 0 9825a 0 0 0 9825a 0 0 0 9825a 499*0
  //   9825a 0 0 0 9825a 0 0 0 9825a 0 0 0 9825a 499*0 9825a 0 0 0 9825a 0 0 0 9825a 0 0 0 9825a 499*0
  //   9825a 0 0 0 9825a 0 0 0 9825a 0 0 0 9825a 499*0 9825a 0 0 0 9825a 0 0 0 9825a 0 0 0 9825a 499*0
  //   9825a 0 0 0 9825a 0 0 0 9825a 0 0 0 9825a 499*0 9825a 0 0 0 9825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
  //   contents of rom_2 (hex, n*v repeats v):
  //   c00 0 0 0 c00 0 0 0 c00 0 0 0 c00 499*0 c00 0 0 0 c00 0 0 0 c00 0 0 0 c00 499*0 c00 0 0 0 c00 0 0 0
  //   c00 0 0 0 c00 499*0 c00 0 0 0 c00 0 0 0 c00 0 0 0 c00 499*0 c00 0 0 0 c00 0 0 0 c00 0 0 0 c00 499*0
  //   c00 0 0 0 c00 0 0 0 c00 0 0 0 c00 499*0 c00 0 0 0 c00 0 0 0 c00 0 0 0 c00 499*0 c00 0 0 0 c00 0 0 0
  //   c00 0 0 0 c00 499*0 c00 0 0 0 c00 0 0 0 c00 0 0 0 c00 499*0 c00 0 0 0 c00 0 0 0 c00 0 0 0 c00 499*0
  //   c00 0 0 0 c00 0 0 0 c00 0 0 0 c00 499*0 c00 0 0 0 c00 0 0 0 c00 0 0 0 c00 499*0 c00 0 0 0 c00 0 0 0
  //   c00 0 0 0 c00 499*0 c00 0 0 0 c00 0 0 0 c00 0 0 0 c00 499*0 c00 0 0 0 c00 0 0 0 c00 0 0 0 c00 499*0
  //   c00 0 0 0 c00 0 0 0 c00 0 0 0 c00 499*0 c00 0 0 0 c00 0 0 0 c00 0 0 0 c00 499*0 c00 0 0 0 c00 0 0 0
  //   c00 0 0 0 c00 499*0 c00 0 0 0 c00 0 0 0 c00 0 0 0 c00 499*0 c00 0 0 0 c00 0 0 0 c00 0 0 0 c00 499*0
  //   c00 0 0 0 c00 0 0 0 c00 0 0 0 c00 499*0 c00 0 0 0 c00 0 0 0 c00 0 0 0 c00 499*0 c00 0 0 0 c00 0 0 0
  //   c00 0 0 0 c00 499*0 c00 0 0 0 c00 0 0 0 c00 0 0 0 c00 499*0 c00 0 0 0 c00 0 0 0 c00 0 0 0 c00 499*0
  //   c00 0 0 0 c00 0 0 0 c00 0 0 0 c00 499*0 c00 0 0 0 c00 0 0 0 c00 0 0 0 c00 499*0 c00 0 0 0 c00 0 0 0
  //   c00 0 0 0 c00 499*0 c00 0 0 0 c00 0 0 0 c00 0 0 0 c00 499*0 c00 0 0 0 c00 0 0 0 c00 0 0 0 c00 499*0
  //   c00 0 0 0 c00 0 0 0 c00 0 0 0 c00 499*0 c00 0 0 0 c00 0 0 0 c00 0 0 0 c00 499*0 c00 0 0 0 c00 0 0 0
  //   c00 0 0 0 c00 499*0 c00 0 0 0 c00 0 0 0 c00 0 0 0 c00 499*0 c00 0 0 0 c00 0 0 0 c00 0 0 0 c00 499*0
  //   c00 0 0 0 c00 0 0 0 c00 0 0 0 c00 499*0 c00 0 0 0 c00 0 0 0 c00 0 0 0 c00 499*0 c00 0 0 0 c00 0 0 0
  //   c00 0 0 0 c00 499*0 c00 0 0 0 c00 0 0 0 c00 0 0 0 c00 499*0 c00 0 0 0 c00 0 0 0 c00 0 0 0 c00 499*0
  //   c00 0 0 0 c00 0 0 0 c00 0 0 0 c00 499*0 c00 0 0 0 c00 0 0 0 c00 0 0 0 c00 499*0 c00 0 0 0 c00 0 0 0
  //   c00 0 0 0 c00 499*0 c00 0 0 0 c00 0 0 0 c00 0 0 0 c00 499*0 c00 0 0 0 c00 0 0 0 c00 0 0 0 c00 499*0
  //   c00 0 0 0 c00 0 0 0 c00 0 0 0 c00 499*0 c00 0 0 0 c00 0 0 0 c00 0 0 0 c00 499*0 c00 0 0 0 c00 0 0 0
  //   c00 0 0 0 c00 499*0 c00 0 0 0 c00 0 0 0 c00 0 0 0 c00 499*0 c00 0 0 0 c00 0 0 0 c00 0 0 0 c00 499*0
  //   c00 0 0 0 c00 0 0 0 c00 0 0 0 c00 499*0 c00 0 0 0 c00 0 0 0 c00 0 0 0 c00 499*0 c00 0 0 0 c00 0 0 0
  //   c00 0 0 0 c00 499*0 c00 0 0 0 c00 0 0 0 c00 0 0 0 c00 499*0 c00 0 0 0 c00 0 0 0 c00 0 0 0 c00 499*0
  //   c00 0 0 0 c00 0 0 0 c00 0 0 0 c00 499*0 c00 0 0 0 c00 0 0 0 c00 0 0 0 c00 499*0 c00 0 0 0 c00 0 0 0
  //   c00 0 0 0 c00 499*0 c00 0 0 0 c00 0 0 0 c00 0 0 0 c00 499*0 c00 0 0 0 c00 0 0 0 c00 0 0 0 c00 499*0
  //   c00 0 0 0 c00 0 0 0 c00 0 0 0 c00 499*0 c00 0 0 0 c00 0 0 0 c00 0 0 0 c00 499*0 c00 0 0 0 c00 0 0 0
  //   c00 0 0 0 c00 499*0 c00 0 0 0 c00 0 0 0 c00 0 0 0 c00 499*0 c00 0 0 0 c00 0 0 0 c00 0 0 0 c00 499*0
  //   c00 0 0 0 c00 0 0 0 c00 0 0 0 c00 499*0 c00 0 0 0 c00 0 0 0 c00 0 0 0 c00 499*0 c00 0 0 0 c00 0 0 0
  //   c00 0 0 0 c00 499*0 c00 0 0 0 c00 0 0 0 c00 0 0 0 c00 499*0 c00 0 0 0 c00 0 0 0 c00 0 0 0 c00 499*0
  //   c00 0 0 0 c00 0 0 0 c00 0 0 0 c00 499*0 c00 0 0 0 c00 0 0 0 c00 0 0 0 c00 499*0 c00 0 0 0 c00 0 0 0
  //   c00 0 0 0 c00 499*0 c00 0 0 0 c00 0 0 0 c00 0 0 0 c00 499*0 c00 0 0 0 c00 0 0 0 c00 0 0 0 c00 499*0
  //   c00 0 0 0 c00 0 0 0 c00 0 0 0 c00 499*0 c00 0 0 0 c00 0 0 0 c00 0 0 0 c00 499*0 c00 0 0 0 c00 0 0 0
  //   c00 0 0 0 c00 499*0 c00 0 0 0 c00 0 0 0 c00 0 0 0 c00 499*0 c00 0 0 0 c00 0 0 0 c00 0 0 0 c00 499*0
  //   c00 0 0 0 c00 0 0 0 c00 0 0 0 c00 499*0 c00 0 0 0 c00 0 0 0 c00 0 0 0 c00 499*0 c00 0 0 0 c00 0 0 0
  //   c00 0 0 0 c00 499*0 c00 0 0 0 c00 0 0 0 c00 0 0 0 c00 499*0 c00 0 0 0 c00 0 0 0 c00 0 0 0 c00 499*0
  //   c00 0 0 0 c00 0 0 0 c00 0 0 0 c00 499*0 c00 0 0 0 c00 0 0 0 c00 0 0 0 c00 499*0 c00 0 0 0 c00 0 0 0
  //   c00 0 0 0 c00 499*0 c00 0 0 0 c00 0 0 0 c00 0 0 0 c00 499*0 c00 0 0 0 c00 0 0 0 c00 0 0 0 c00 499*0
  //   c00 0 0 0 c00 0 0 0 c00 0 0 0 c00 499*0 c00 0 0 0 c00 0 0 0 c00 0 0 0 c00 499*0 c00 0 0 0 c00 0 0 0
  //   c00 0 0 0 c00 499*0 c00 0 0 0 c00 0 0 0 c00 0 0 0 c00 499*0 c00 0 0 0 c00 0 0 0 c00 0 0 0 c00 499*0
  //   c00 0 0 0 c00 0 0 0 c00 0 0 0 c00 499*0 c00 0 0 0 c00 0 0 0 c00 0 0 0 c00 499*0 c00 0 0 0 c00 0 0 0
  //   c00 0 0 0 c00 499*0 c00 0 0 0 c00 0 0 0 c00 0 0 0 c00 499*0 c00 0 0 0 c00 0 0 0 c00 0 0 0 c00 499*0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
endmodule

module datapath (
  input  [5:0] ALUF,
  input  [3:0] IB,
  input  [1:0] ALUCIN,
  input  [7:0] DIN,
  input  [2:0] ABL,
  input  PC_1,
  input  [3:0] OB,
  input  [2:0] ABH,
  input  [9:0] FLAGS,
  output [7:0] DOUT,
  output [7:0] ABL_2,
  output [7:0] ABH_2,
  output [7:0] PREG
);

  wire ALUN, ALUV, ALUZ, clock_1_out, decoder_1_out1, decoder_1_out2, decoder_1_out3, decoder_1_out4,
       decoder_1_out5, decoder_1_out6, decoder_1_out7, decoder_1_out8, decoder_1_out9, decoder_1_out10,
       decoder_2_out0, decoder_2_out1, decoder_2_out2, decoder_2_out3, decoder_2_out4, decoder_3_out0,
       decoder_3_out1, decoder_3_out2, decoder_3_out3, decoder_3_out4, decoder_3_out5, decoder_3_out6,
       decoder_3_out7, decoder_3_out8, decoder_3_out9, decoder_3_out10, decoder_4_out0, decoder_4_out1,
       decoder_4_out2, decoder_4_out3, decoder_4_out4, multiplexer_1_out, PCL_carry;
  wire [7:0] A_q, AH_q, AL_q, alu_1_y, D_q, PCH_q, PCL_q, S_q, X_q, Y_q;

  Multiplexer #(.select(2), .enable("false")) multiplexer_1 (
    .in0(1'b0), .in1(1'b1), .in2(PREG[0]), .in3(PREG[0]), .out(multiplexer_1_out), .sel(ALUCIN));
  Decoder #(.select(4), .enable("false")) decoder_1 (
    .out1(decoder_1_out1), .out2(decoder_1_out2), .out3(decoder_1_out3), .out4(decoder_1_out4),
    .out5(decoder_1_out5), .out6(decoder_1_out6), .out7(decoder_1_out7), .out8(decoder_1_out8),
    .out9(decoder_1_out9), .out10(decoder_1_out10), .sel(OB));  // open: out0, out11, out12, out13, out14, out15
  alu alu_1 (
    .A(DOUT), .B(DIN), .F(ALUF), .Cin(multiplexer_1_out), .Cout(PREG[3]), .N(ALUN), .V(ALUV), .Z(ALUZ),
    .Y(alu_1_y));
  // Probe on alu_1_y
  Clock clock_1 (.out(clock_1_out));
  Register A (.D(alu_1_y), .en(decoder_1_out1), .Q(A_q), .clk(clock_1_out));  // open: clr
  Register X (.D(alu_1_y), .en(decoder_1_out2), .Q(X_q), .clk(clock_1_out));  // open: clr
  Register Y (.D(alu_1_y), .en(decoder_1_out3), .Q(Y_q), .clk(clock_1_out));  // open: clr
  Register AL (.D(alu_1_y), .en(decoder_1_out4), .Q(AL_q), .clk(clock_1_out));  // open: clr
  Register AH (.D(alu_1_y), .en(decoder_1_out5), .Q(AH_q), .clk(clock_1_out));  // open: clr
  Register S (.D(alu_1_y), .en(decoder_1_out6), .Q(S_q), .clk(clock_1_out));  // open: clr
  Counter PCL (
    .load(decoder_1_out7), .D(alu_1_y), .count(PC_1), .Q(PCL_q), .carry(PCL_carry), .clk(clock_1_out));  // open: clr
  Counter PCH (
    .load(decoder_1_out8), .D(alu_1_y), .count(PCL_carry), .Q(PCH_q), .clk(clock_1_out));  // open: carry, clr
  Register D (.D(alu_1_y), .en(decoder_1_out9), .Q(D_q), .clk(clock_1_out));  // open: clr
  flag C (.ALUF(PREG[3]), .BUSP(alu_1_y[0]), .LOAD(decoder_1_out10), .OP(FLAGS[1:0]), .VAL(PREG[0]));
  flag Z (.ALUF(ALUZ), .BUSP(alu_1_y[1]), .LOAD(decoder_1_out10), .OP(FLAGS[3:2]), .VAL(PREG[1]));
  flag I (.BUSP(alu_1_y[2]), .LOAD(decoder_1_out10), .OP(FLAGS[5:4]), .VAL(PREG[2]));  // open: ALUF
  flag V (.ALUF(ALUV), .BUSP(alu_1_y[6]), .LOAD(decoder_1_out10), .OP(FLAGS[7:6]), .VAL(PREG[6]));
  flag N (.ALUF(ALUN), .BUSP(alu_1_y[7]), .LOAD(decoder_1_out10), .OP(FLAGS[9:8]), .VAL(PREG[7]));
  assign DOUT = decoder_3_out0 ? {8{1'b0}} : 8'bz;  // Controlled_Buffer controlled_buffer_1
  assign DOUT = decoder_3_out1 ? A_q : 8'bz;  // Controlled_Buffer controlled_buffer_2
  assign DOUT = decoder_3_out2 ? X_q : 8'bz;  // Controlled_Buffer controlled_buffer_3
  assign DOUT = decoder_3_out3 ? Y_q : 8'bz;  // Controlled_Buffer controlled_buffer_4
  assign DOUT = decoder_3_out4 ? AL_q : 8'bz;  // Controlled_Buffer controlled_buffer_5
  assign DOUT = decoder_3_out5 ? AH_q : 8'bz;  // Controlled_Buffer controlled_buffer_6
  assign DOUT = decoder_3_out6 ? S_q : 8'bz;  // Controlled_Buffer controlled_buffer_7
  assign DOUT = decoder_3_out7 ? PCL_q : 8'bz;  // Controlled_Buffer controlled_buffer_8
  assign DOUT = decoder_3_out8 ? PCH_q : 8'bz;  // Controlled_Buffer controlled_buffer_9
  assign DOUT = decoder_3_out9 ? D_q : 8'bz;  // Controlled_Buffer controlled_buffer_10
  assign DOUT = decoder_3_out10 ? {PREG[7:6], 3'b000, PREG[2:0]} : 8'bz;  // Controlled_Buffer controlled_buffer_11
  assign ABL_2 = decoder_4_out1 ? AL_q : 8'bz;  // Controlled_Buffer controlled_buffer_12
  assign ABH_2 = decoder_2_out1 ? AH_q : 8'bz;  // Controlled_Buffer controlled_buffer_13
  assign ABL_2 = decoder_4_out2 ? S_q : 8'bz;  // Controlled_Buffer controlled_buffer_14
  assign ABL_2 = decoder_4_out0 ? PCL_q : 8'bz;  // Controlled_Buffer controlled_buffer_15
  assign ABH_2 = decoder_2_out0 ? PCH_q : 8'bz;  // Controlled_Buffer controlled_buffer_16
  Decoder #(.select(3), .enable("false")) decoder_2 (
    .out0(decoder_2_out0), .out1(decoder_2_out1), .out2(decoder_2_out2), .out3(decoder_2_out3),
    .out4(decoder_2_out4), .sel(ABH));  // open: out5, out6, out7
  Decoder #(.select(4), .enable("false")) decoder_3 (
    .out0(decoder_3_out0), .out1(decoder_3_out1), .out2(decoder_3_out2), .out3(decoder_3_out3),
    .out4(decoder_3_out4), .out5(decoder_3_out5), .out6(decoder_3_out6), .out7(decoder_3_out7),
    .out8(decoder_3_out8), .out9(decoder_3_out9), .out10(decoder_3_out10), .sel(IB));  // open: out11, out12, out13, out14, out15
  Decoder #(.select(3), .enable("false")) decoder_4 (
    .out0(decoder_4_out0), .out1(decoder_4_out1), .out2(decoder_4_out2), .out3(decoder_4_out3),
    .out4(decoder_4_out4), .sel(ABL));  // open: out5, out6, out7
  assign ABH_2 = decoder_2_out3 ? {8{1'b0}} : 8'bz;  // Controlled_Buffer controlled_buffer_17
  assign ABH_2 = decoder_2_out2 ? 8'h1 : 8'bz;  // Controlled_Buffer controlled_buffer_18
  assign ABH_2 = decoder_2_out4 ? {8{1'b1}} : 8'bz;  // Controlled_Buffer controlled_buffer_19
  assign ABL_2 = decoder_4_out3 ? 8'hfc : 8'bz;  // Controlled_Buffer controlled_buffer_20
  assign ABL_2 = decoder_4_out4 ? 8'hfe : 8'bz;  // Controlled_Buffer controlled_buffer_21

  assign PREG[5:4] = 2'b00;

  // Other names for the same wires on the sheet: CF = PREG[0]; ALUC = PREG[3]
endmodule

module alu (
  input  [5:0] F,
  input  Cin,
  input  [7:0] A,
  input  [7:0] B,
  output [7:0] Y,
  output N,
  output Z,
  output Cout,
  output V
);

  wire n181_1_cn_4, n181_2_cn_4, not_1_out, not_2_out, xnor_1_out, xor_1_out, xor_2_out;
  wire [7:0] n181_1_f0;

  not not_1 (not_1_out, Cin);
  _181 u_181_1 (
    .A0(A[0]), .B0(B[0]), .A1(A[1]), .B1(B[1]), .A2(A[2]), .B2(B[2]), .A3(A[3]), .B3(B[3]),
    .F0(n181_1_f0[0]), .F1(n181_1_f0[1]), .F2(n181_1_f0[2]), .F3(n181_1_f0[3]), .Cn(not_1_out), .M(F[4]),
    .S0(F[0]), .S1(F[1]), .S2(F[2]), .S3(F[3]), .Cn_4(n181_1_cn_4));  // open: A_B, P, G
  _181 u_181_2 (
    .A0(A[4]), .B0(B[4]), .A1(A[5]), .B1(B[5]), .A2(A[6]), .B2(B[6]), .A3(A[7]), .B3(B[7]),
    .F0(n181_1_f0[4]), .F1(n181_1_f0[5]), .F2(n181_1_f0[6]), .F3(n181_1_f0[7]), .Cn(n181_1_cn_4), .M(F[4]),
    .S0(F[0]), .S1(F[1]), .S2(F[2]), .S3(F[3]), .Cn_4(n181_2_cn_4));  // open: A_B, P, G
  not not_2 (not_2_out, n181_2_cn_4);
  xor xor_1 (xor_1_out, F[2], B[7]);
  Multiplexer #(.enable("false")) multiplexer_1 (.in0(not_2_out), .in1(A[0]), .out(Cout), .sel(F[5]));
  xor xor_2 (xor_2_out, n181_1_f0[7], A[7]);
  Multiplexer #(.width(8), .enable("false")) multiplexer_2 (
    .in0(n181_1_f0), .in1({Cin, A[7:1]}), .out({N, Y[6:0]}), .sel(F[5]));
  xnor xnor_1 (xnor_1_out, A[7], xor_1_out);
  and and_1 (V, xnor_1_out, xor_2_out);
  nor nor_1 (Z, N, Y[6], Y[5], Y[4], Y[3], Y[2], Y[1], Y[0]);

  assign Y[7] = N;
endmodule

module _181 (
  input  A0,
  input  B0,
  input  A1,
  input  B1,
  input  A2,
  input  B2,
  input  A3,
  input  B3,
  input  Cn,
  input  M,
  input  S0,
  input  S1,
  input  S2,
  input  S3,
  output P,
  output G,
  output Cn_4,
  output F0,
  output F1,
  output F2,
  output F3,
  output A_B
);

  wire and_1_out, and_2_out, and_3_out, and_4_out, and_5_out, and_6_out, and_7_out, and_8_out, and_9_out,
       and_10_out, and_12_out, and_13_out, and_14_out, and_15_out, and_16_out, and_17_out, and_18_out,
       and_19_out, and_20_out, and_21_out, and_22_out, and_23_out, and_24_out, and_25_out, and_26_out,
       and_27_out, and_28_out, and_29_out, and_30_out, and_31_out, and_32_out, and_33_out, nand_1_out,
       nand_3_out, nor_1_out, nor_2_out, nor_3_out, nor_4_out, nor_5_out, nor_6_out, nor_7_out, nor_8_out,
       nor_9_out, nor_10_out, nor_11_out, not_1_out, not_2_out, not_3_out, not_4_out, not_5_out, not_6_out,
       not_7_out, not_8_out, not_9_out;

  not not_1 (not_1_out, M);
  nand nand_1 (nand_1_out, Cn, not_1_out);
  xor xor_1 (F0, nand_1_out, and_2_out);
  and and_1 (and_1_out, B0, S0);
  nor nor_1 (nor_1_out, A0, and_1_out, and_3_out);
  not not_2 (not_2_out, nor_1_out);
  and and_2 (and_2_out, not_2_out, nor_3_out);
  not not_3 (not_3_out, B0);
  and and_3 (and_3_out, S1, not_3_out);
  and and_4 (and_4_out, not_1_out, nor_3_out, Cn);
  and and_5 (and_5_out, not_1_out, nor_1_out);
  nor nor_2 (nor_2_out, and_5_out, and_4_out);
  xor xor_2 (F1, nor_2_out, and_10_out);
  and and_6 (and_6_out, A0, B0, S3);
  and and_7 (and_7_out, not_3_out, S2, A0);
  nor nor_3 (nor_3_out, and_7_out, and_6_out);
  and and_8 (and_8_out, B1, S0);
  nor nor_4 (nor_4_out, A1, and_8_out, and_12_out);
  and and_9 (and_9_out, not_1_out, nor_4_out);
  not not_4 (not_4_out, nor_4_out);
  and and_10 (and_10_out, not_4_out, nor_6_out);
  and and_11 (A_B, F0, F1, F2, F3);
  not not_5 (not_5_out, B1);
  and and_12 (and_12_out, S1, not_5_out);
  and and_13 (and_13_out, not_1_out, nor_1_out, nor_6_out);
  nor nor_5 (nor_5_out, and_9_out, and_13_out, and_16_out);
  xor xor_3 (F2, nor_5_out, and_19_out);
  and and_14 (and_14_out, A1, B1, S3);
  and and_15 (and_15_out, not_5_out, S2, A1);
  nor nor_6 (nor_6_out, and_15_out, and_14_out);
  and and_16 (and_16_out, not_1_out, Cn, nor_3_out, nor_6_out);
  and and_17 (and_17_out, B2, S0);
  nor nor_7 (nor_7_out, A2, and_17_out, and_20_out);
  and and_18 (and_18_out, not_1_out, nor_7_out);
  not not_6 (not_6_out, nor_7_out);
  and and_19 (and_19_out, not_6_out, nor_9_out);
  not not_7 (not_7_out, B2);
  and and_20 (and_20_out, S1, not_7_out);
  and and_21 (and_21_out, not_1_out, nor_4_out, nor_9_out);
  nor nor_8 (nor_8_out, and_18_out, and_21_out, and_24_out, and_25_out);
  xor xor_4 (F3, nor_8_out, and_28_out);
  and and_22 (and_22_out, not_7_out, S2, A2);
  and and_23 (and_23_out, A2, B2, S3);
  nor nor_9 (nor_9_out, and_22_out, and_23_out);
  and and_24 (and_24_out, not_1_out, nor_1_out, nor_6_out, nor_9_out);
  and and_25 (and_25_out, not_1_out, Cn, nor_3_out, nor_6_out, nor_9_out);
  and and_26 (and_26_out, B3, S0);
  nor nor_10 (nor_10_out, A3, and_26_out, and_27_out);
  not not_8 (not_8_out, B3);
  and and_27 (and_27_out, S1, not_8_out);
  not not_9 (not_9_out, nor_10_out);
  nand nand_2 (P, nor_3_out, nor_6_out, nor_9_out, nor_11_out);
  and and_28 (and_28_out, not_9_out, nor_11_out);
  and and_29 (and_29_out, not_8_out, S2, A3);
  and and_30 (and_30_out, A3, B3, S3);
  nor nor_11 (nor_11_out, and_29_out, and_30_out);
  nand nand_3 (nand_3_out, Cn, nor_3_out, nor_6_out, nor_9_out, nor_11_out);
  and and_31 (and_31_out, nor_4_out, nor_9_out, nor_11_out);
  and and_32 (and_32_out, nor_1_out, nor_6_out, nor_9_out, nor_11_out);
  nand nand_4 (Cn_4, nand_3_out, G);
  and and_33 (and_33_out, nor_7_out, nor_11_out);
  nor nor_12 (G, and_32_out, and_31_out, and_33_out, nor_10_out);
endmodule

module flag (
  input  ALUF,
  input  BUSP,
  input  LOAD,
  input  [1:0] OP,
  output VAL
);

  wire clock_1_out, multiplexer_1_out;

  Clock clock_1 (.out(clock_1_out));
  Multiplexer #(.select(3), .enable("false")) multiplexer_1 (
    .in0(VAL), .in1(ALUF), .in2(1'b1), .in3(1'b0), .in4(BUSP), .in5(BUSP), .in6(BUSP), .in7(BUSP),
    .out(multiplexer_1_out), .sel({LOAD, OP}));
  D_Flip_Flop d_ff_1 (.clk(clock_1_out), .D(multiplexer_1_out), .Q(VAL));  // open: Qn, preset, en, reset
endmodule
